// Logisim project overflow_circuit.circ as structural Verilog: 1 circuit, main circuit main
module main (
  input  S7,
  input  A7,
  input  B7,
  output V
);

  wire and_1_out, nand_1_out, nor_1_out, nor_2_out;

  nor nor_1 (nor_1_out, A7, B7);
  nand nand_1 (nand_1_out, A7, B7);
  and and_1 (and_1_out, S7, nor_1_out);
  nor nor_2 (nor_2_out, S7, nand_1_out);
  or or_1 (V, and_1_out, nor_2_out);
endmodule
